# Fritzing sketch Schematic (saved by Fritzing 0.9.4)
breadboards: 1

parts:
  WeMos_D1_Mini1 = WeMos D1 Mini
  Part1 = HX711 Weighing Sensor Module
  LED1 = LEDs [package=led10mm]
  S1 = Pushbutton [package="[THT]"]
  LED_on_ESP12 = LEDs [package=led10mm]

nets:
  5V: WeMos_D1_Mini1.5V, Part1.VCC
  N1: WeMos_D1_Mini1.D0, LED_on_ESP12.A
  N2: WeMos_D1_Mini1.D2, Part1.DO/RX
  N3: WeMos_D1_Mini1.D3, Part1.CK/TX
  N4: WeMos_D1_Mini1.D4, LED1.A
  N5: WeMos_D1_Mini1.RST, S1.Pin_3, S1.Pin_4
  GND: Part1.GND, LED1.C, S1.Pin_1, S1.Pin_2, LED_on_ESP12.C
  To scale: Part1.E+, Part1.E-, Part1.A+, Part1.A-
